# Fritzing sketch FindMeBasev2 (saved by Fritzing 0.9.3b)
breadboards: 1

parts:
  Raspberry_Pi1 = Raspberry Pi B+
  Componente1 = Logic Level Converter
  U2 = PIC16F84-DIP [package=dil18]
  U4 = RF-LINK_RX [package=rf-link_rx]
  ANT1 = Antenna
  C1 = Capacitor Polarized [package=nippon_f80]
  C2 = Capacitor Polarized [package=nippon_f80]

nets:
  N1: Raspberry_Pi1.3v3, Componente1.LV
  GND: Raspberry_Pi1.GND, Componente1.GND, U2.VSS, U4.GND, C1.-, C2.-
  N2: Raspberry_Pi1.GPIO15, Componente1.RX_LV
  N3: Raspberry_Pi1.GPIO14, Componente1.TX_LV
  5V: Raspberry_Pi1.5V, Componente1.HV, U2.VDD, C1.+
  N4: Componente1.TX_HV, U2.RB1_SDA
  N5: Componente1.RX_HV, U2.RB2_RX
  N6: U2.RA0_AN0, U4.DATA
  N7: U4.+5V, C2.+
  N8: U4.ANT, ANT1.antenna_lead

custom parts:
  PIC16F84-DIP: 8-bit PIC uC
