# Fritzing sketch FindMeSmartBagv4 (saved by Fritzing 0.9.3b)

parts:
  U1 = ESP8266 WiFi Module [part_number=ESP8266]
  U3 = LIPO-1000mAh [package=lipo-1000]
  Componente1 = USB LiPoly Charger
  S1 = Square Pushbutton
  R2 = Resistor [tolerance=±5% resistance=10k package="2010 [SMD]"]
  U5 = V_REG_LD1117VXX [package=78xxl]
  SG1 = Buzzer 12mm [package=buzzer-ccv]
  C1 = Capacitor Polarized [package=cpol-radial-100uf-25v]
  R3 = Resistor [tolerance=±5% resistance=220 package="2010 [SMD]"]
  R4 = Resistor [tolerance=±5% resistance=10k package="2010 [SMD]"]
  LED1 = smd LED [color="Red (633nm)" package="1206 [SMD]"]
  Q2 = PNP-Transistor [package="TO92 [THT]"]

nets:
  N1: U1.VCC, R3.Pin_1
  N2: U1.GPIO_0, R4.Pin_0, Q2.C
  N3: U1.GPIO_2, S1.leg1, R2.Pin_0
  N4: U1.CH_PD, R2.Pin_1, U5.OUT
  GND: U1.GND, U3.-, Componente1.GND, S1.leg0, U5.GND, C1.-
  N5: U3.+, Componente1.VBAT, U5.IN, SG1.2
  N6: SG1.1, Q2.B
  N7: C1.+, R4.Pin_1
  N8: R3.Pin_0, LED1.anode

custom parts:
  ESP8266 WiFi Module: Generic WiFi Module based on the ESP8266 with onboard PCB antenna and UART communications
