# Fritzing sketch myRFButton v3 (saved by Fritzing 0.9.3b)

parts:
  U1 = mystery part, 18 pins [chip_label=PIC16f84a spacing=300mil]
  BAT1 = Battery Holders [package=battcon_245mm_pth]
  U2 = RF-LINK_TX [package=rf-link_tx]
  S1 = Round Pushbutton

nets:
  N1: U1.pin5, BAT1.+, U2.GND
  N2: U1.pin14, U2.+5V, S1.leg0
  N3: U1.pin17, U2.DATA
  N4: BAT1.-, S1.leg1

// code stored in the sketch: DC_Motor_controller_spinning.pde
int potpin = A0;
int val;

void setup() {}

void loop() {
val = analogRead(potpin);
val = map(val, 0, 1023, 0, 225);
analogWrite(3, val);
delay(15);
}
